# Fritzing sketch perf-shift-register (saved by Fritzing 0.9.3b)
perfboards: 1

parts:
  Part1 = Adafruit Metro M0 Express
  U1 = 74HC595 [package="DIP16 [THT]"]
  Part2 = EasyDriver_v44 [part_number=TB6600]
  U2 = 74HC165 [part_number=SN74LS165 package="DIP16 [THT]"]
  S1 = Round Pushbutton [part_number=Limit1]
  Part3 = EasyDriver_v44 [part_number=TB6600]
  S2 = Round Pushbutton [part_number=Limit1]
  R3 = Vertical Resistor [tolerance=±5% resistance=10k package=THT]
  JP24 = Header 1 [package=1x01_offset]
  JP33 = Header 1 [package=1x01_offset]  # not connected
  JP36 = Header 1 [package=1x01_offset]
  JP50 = Header 1 [package=1x01_offset]
  J4 = Camdenboss CTB0158-3 [part_number=CTB0158-3 package=THT]
  J5 = Camdenboss CTB0158-3 [part_number=CTB0158-3 package=THT]
  J6 = Camdenboss CTB0158-3 [part_number=CTB0158-3 package=THT]
  J7 = Camdenboss CTB0158-3 [part_number=CTB0158-3 package=THT]
  J8 = Camdenboss CTB0158-3 [part_number=CTB0158-3 package=THT]
  R10 = Resistor [tolerance=±5% resistance=10k package=THT]
  R11 = Resistor [tolerance=±5% resistance=10k package=THT]
  R12 = Resistor [tolerance=±5% resistance=10k package=THT]
  R13 = Resistor [tolerance=±5% resistance=10k package=THT]
  J9 = MAGJACK [package=magjack]
  J10 = MAGJACK [package=magjack]
  J11 = MAGJACK [package=magjack]
  J12 = MAGJACK [package=magjack]
  C1 = Ceramic Capacitor [capacitance=100nF package="100 mil [THT, multilayer]"]

nets:
  LOW: Part1.A4
  FakeLimitSwitches: Part1.A5
  MISO: Part1.MISO, U2.Q7', J9.TD-, J9.YLED+
  CLK: Part1.SCK, U1.SH_CP, U2.Q2, J9.GLED-, J10.TCT
  MOSI: Part1.MOSI, U1.DS, J9.TCT, J9.TD+
  GND: Part1.GND, U1.GND, U1.OE, Part2.GND, U2.GND, U2.Q0, S1.leg1, Part3.GND, S2.leg1, R3.Pin_1, J4.pin2, J11.TCT, J12.GLED-, C1.1
  LATCH: Part1.D12, U1.ST_CP, J9.YLED-, J9.GLED+, J10.TD+, J10.TD-
  SH/LD: Part1.D11, U2.Q1, JP50.1, J11.TD+, J11.TD-, J12.YLED-, J12.GLED+
  EN: Part1.D10, Part2.ENABLE, Part3.ENABLE, R3.Pin_0
  3.3V: Part1.3.3V, U1.MR, U1.VCC, Part2.VCC, U2.VCC, Part3.VCC, JP24.1, J4.pin3, R11.Pin_1, R13.Pin_1, J11.GLED+, J11.GLED-, J12.TCT, J12.TD+, C1.0
  N1: U1.Q1, Part2.STEP, J5.pin2
  N2: U1.Q2, Part3.DIR, J6.pin3
  N3: U1.Q3, Part3.SLEEP, J6.pin2
  N4: U1.Q4, J7.pin3
  N5: U1.Q5, J7.pin2
  N6: U1.Q6, J8.pin3
  N7: U1.Q7, J8.pin2
  N8: U1.Q7', J10.GLED+, J10.GLED-
  N9: U1.Q0, Part2.DIR, J5.pin3
  24V: Part2.V+, Part3.V+
  Limit2: U2.Q3, J7.pin1, R11.Pin_0
  Limit3: U2.Q5, J8.pin1, R13.Pin_0
  SER in: U2.MR, J10.YLED+, J10.YLED-
  Limit0: U2.SH_CP, S1.leg0, J5.pin1, R12.Pin_1
  Limit1: U2.OE, S2.leg0, J6.pin1, R10.Pin_1
  N10: JP36.1, J4.pin1, J11.YLED+, J11.YLED-, J12.TD-, J12.YLED+

notes:
  add header oles
  can swap 2&15
  White - bridge
  grey - lead
  +
  -
  EN
  shield GND
  All RJ45:
  short pairs together
  M1 Dir
  Step
  Limit
  M2
  Dir Step Limit
  M3 Limit
  Step
  Dir
  M4
  40x30
  -
  Latch Out
  EN
  +
  CLK
  Latch In
  MISO
  MOSI

custom parts:
  Adafruit Metro M0 Express: Metro is our series of microcontroller boards for use with the Arduino IDE. This new Metro board looks a whole lot like our original Metro 328, but with a huge upgrade. Instead of the ATmega328, this Metro features a ATSAMD21G18 chip, an ARM Cortex M0+. It's our first Metro that is designed for use with CircuitPython! CircuitPython is our beginner-oriented flavor of MicroPython - and as the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
  74HC165: 8-bit parallel-load shift registers
  Vertical Resistor: A generic resistor (0.25W)
